# Fritzing sketch 7805 Assembly (saved by Fritzing 0.9.3b)
circuit board: 1.85262cm x 5.42577cm
breadboards: 1

parts:
  C1 = Ceramic Capacitor [capacitance=10µF voltage=50V package="100 mil [THT, multilayer]"]
  C2 = Ceramic Capacitor [capacitance=10µF voltage=50V package="100 mil [THT, multilayer]"]
  LED1 = LED - 5mm [color="Red (633nm)" package="5 mm [THT]"]
  R1 = Resistor [tolerance=±5% resistance=220 package=THT]
  J1 = male pin header, 3 pins [form="♂ (male)"]
  U1 = Voltage Regulator - 5V [package="TO220 [THT]"]
  U2 = Voltage Regulator - 5V [package="TO220 [THT]"]
  U3 = Voltage Regulator - 5V [package="TO220 [THT]"]
  U4 = Voltage Regulator - 5V [package="TO220 [THT]"]

nets:
  GND: C1.0, C2.0, R1.Pin_0, J1.pin2, U1.GND, U2.GND, U3.GND, U4.GND
  N1: C1.1, J1.pin1, U1.input_voltage, U2.input_voltage, U3.input_voltage, U4.input_voltage
  N2: C2.1, LED1.anode, J1.pin3, U1.output_voltage, U2.output_voltage, U3.output_voltage, U4.output_voltage
  N3: LED1.cathode, R1.Pin_1

notes:
  7805 Assembly V.0
