# Fritzing sketch Top (saved by Fritzing 0.9.3b)
circuit board: 7.23695cm x 8.88573cm
breadboards: 1

parts:
  TO_BOTTOM = DB25M
  USB1 = USB Connectors [package=usb-a-s-nosilk]
  J1 = double row male pin header, 4 pins [form="♂ (male)"]
  TRS1 = Audio Jack (TRS) 3.5mm [package="4Ucon 08780 [THT]"]
  J_HOR = Basic Servo
  J_VER = Basic Servo
  CONN1 = male pin header, 8 pins [form="♂ (male)"]
  CONN4 = male pin header, 8 pins [form="♂ (male)"]
  CONN3 = male pin header, 8 pins [form="♂ (male)"]
  CONN2 = male pin header, 8 pins [form="♂ (male)"]
  U1 = atmega328 [package=dip]
  7_Segment1 = 7 Segment Display

nets:
  GND: TO_BOTTOM.pin1, USB1.GND, TRS1.Sleeve, J_HOR.gnd, J_VER.gnd, CONN1.pin1, CONN1.pin8, CONN4.pin1, CONN4.pin8, CONN3.pin1, CONN3.pin8, CONN2.pin1, CONN2.pin8, U1.GND, 7_Segment1.common_cathode
  N1: TO_BOTTOM.pin2, J_HOR.pulse
  N2: TO_BOTTOM.pin3, J_VER.pulse
  N3: TO_BOTTOM.pin4, CONN1.pin3, CONN1.pin6, CONN4.pin3, CONN4.pin6, CONN3.pin3, CONN3.pin6, CONN2.pin3, CONN2.pin6, U1.A4
  N4: TO_BOTTOM.pin5, CONN1.pin2, CONN1.pin7, CONN4.pin2, CONN4.pin7, CONN3.pin2, CONN3.pin7, CONN2.pin2, CONN2.pin7, U1.A5
  N5: TO_BOTTOM.pin6, J1.pin1
  N6: TO_BOTTOM.pin7, J1.pin4
  N7: TO_BOTTOM.pin8, TRS1.Ring
  N8: TO_BOTTOM.pin9, TRS1.Tip
  N9: TO_BOTTOM.pin14, USB1.VBUS, CONN1.pin4, CONN1.pin5, CONN4.pin4, CONN4.pin5, CONN3.pin4, CONN3.pin5, CONN2.pin4, CONN2.pin5
  N10: USB1.D+, J1.pin3
  N11: USB1.D-, J1.pin2
  VCC: J_HOR.vcc, J_VER.vcc, U1.VCC
  N12: U1.D2, 7_Segment1.Segment_A
  N13: U1.D3_(PWM), 7_Segment1.Segment_B
  N14: U1.D4, 7_Segment1.Segment_C
  N15: U1.D5_(PWM), 7_Segment1.Segment_D
  N16: U1.D6_(PWM), 7_Segment1.Segment_E
  N17: U1.D7, 7_Segment1.Segment_F
  N18: U1.D8, 7_Segment1.Segment_G
  N19: U1.D9_(PWM), 7_Segment1.Segment_DP

notes:
  D+   D-
  0V SCL SDA 5V 5V SDA SCL 0V
  Circuit V.0
  Top Robot
